# Fritzing sketch schematic (saved by Fritzing 0.9.2b)
circuit board: 8.46667cm x 5.64444cm

parts:
  Part1 = Arduino Pro Mini v13
  LED1 = LED - 5mm [color="Red (633nm)" package="5 mm [THT]"]
  LED2 = LED - 5mm [color="Red (633nm)" package="5 mm [THT]"]
  LED3 = LED - 5mm [color="Red (633nm)" package="5 mm [THT]"]
  LED4 = LED - 5mm [color="Red (633nm)" package="5 mm [THT]"]
  LED5 = LED - 5mm [color="Red (633nm)" package="5 mm [THT]"]
  LED6 = LED - 5mm [color="Red (633nm)" package="5 mm [THT]"]
  LED7 = LED - 5mm [color="Red (633nm)" package="5 mm [THT]"]
  R1 = Resistor [tolerance=±5% resistance=220 package=THT]
  R2 = Resistor [tolerance=±5% resistance=220 package=THT]
  R3 = Resistor [tolerance=±5% resistance=220 package=THT]
  R4 = Resistor [tolerance=±5% resistance=220 package=THT]
  R5 = Resistor [tolerance=±5% resistance=220 package=THT]
  R6 = Resistor [tolerance=±5% resistance=220 package=THT]
  R7 = Resistor [tolerance=±5% resistance=220 package=THT]
  R8 = Resistor [tolerance=±5% resistance=1M package=THT]
  U3 = CAPSENSE_PAD [package=capsense_pad]
  VCC1 = Battery block 9V

nets:
  N1: Part1.RAW, VCC1.+
  GND: Part1.GND, LED1.cathode, LED2.cathode, LED3.cathode, LED4.cathode, LED5.cathode, LED6.cathode, LED7.cathode, VCC1.-
  N2: Part1.D12/MISO, R7.Pin_0
  N3: Part1.D11_PWM/MOSI, R6.Pin_0
  N4: Part1.D10_PWM/SS, R5.Pin_0
  N5: Part1.D9_PWM, R4.Pin_0
  N6: Part1.D8, R3.Pin_0
  N7: Part1.D7, R2.Pin_0
  N8: Part1.D6_PWM, R1.Pin_0
  N9: Part1.D4, R8.Pin_0
  N10: Part1.D3_PWM, R8.Pin_1, U3.RECEIVE, U3.RES
  N11: LED1.anode, R1.Pin_1
  N12: LED2.anode, R2.Pin_1
  N13: LED3.anode, R3.Pin_1
  N14: LED4.anode, R7.Pin_1
  N15: LED5.anode, R6.Pin_1
  N16: LED6.anode, R5.Pin_1
  N17: LED7.anode, R4.Pin_1

// code stored in the sketch: dice.ino
/*
Arduino based DICE with touch sensor

Connect Capacitive touch sensor 1Mohm resistor send and recv pins
Connect 7 led pins 220ohm resistor to arduino digital pins.

dice_pins array

*0     *3
*1  *6 *4
*2     *5

avoime@gmail.com 2016
git@github.com:voime/arduinoDice.git

*/

#include <CapacitiveSensor.h>

// pins setup and creating objects

// Mega board testing
//int dice_pins[] = {22, 24, 26, 28, 30, 32, 34 };
//CapacitiveSensor cs = CapacitiveSensor(41,45);

// Arduino Pro mini
int dice_pins[] = {12, 11, 10, 6, 7, 8, 9 };
CapacitiveSensor cs = CapacitiveSensor(4,3);

int max_touch = 10; 

// for nice spinner
int spin_start = 250;
int spin_time;
int spin_step = 0;

boolean show_dice = false;

int value = 0;

void setup(){
  
}

void loop(){

    int touch =  cs.capacitiveSensor(30);
    
    if (touch > max_touch) {
      
      spin();
      value = random(1,7);
    
    } else {
    
      if (show_dice){
        spin_time = spin_start;
        dice(value);
      }
    
    }
    
    delay(10);

}

// nice spinner, if holding finger down
void spin()
{
  
  if (spin_time > 50){
    spin_time = spin_time - 20;
  } 
    
  if (spin_step==0){
    
    digitalWrite(dice_pins[0], HIGH);
    digitalWrite(dice_pins[1], LOW);
    digitalWrite(dice_pins[2], LOW);
    digitalWrite(dice_pins[3], LOW);
    digitalWrite(dice_pins[4], LOW);
    digitalWrite(dice_pins[5], HIGH);
    digitalWrite(dice_pins[6], LOW);    
    
    spin_step = 1;

  }else if (spin_step==1){
    digitalWrite(dice_pins[0], LOW);
    digitalWrite(dice_pins[1], HIGH);
    digitalWrite(dice_pins[2], LOW);
    digitalWrite(dice_pins[3], LOW);
    digitalWrite(dice_pins[4], HIGH);
    digitalWrite(dice_pins[5], LOW);
    digitalWrite(dice_pins[6], LOW);    
    
    spin_step = 2;

  }else if(spin_step==2){

    digitalWrite(dice_pins[0], LOW);
    digitalWrite(dice_pins[1], LOW);
    digitalWrite(dice_pins[2], HIGH);
    digitalWrite(dice_pins[3], HIGH);
    digitalWrite(dice_pins[4], LOW);
    digitalWrite(dice_pins[5], LOW);    
    digitalWrite(dice_pins[6], LOW);
    
    spin_step = 3;

  }else{

    digitalWrite(dice_pins[0], LOW);
    digitalWrite(dice_pins[1], LOW);
    digitalWrite(dice_pins[2], LOW);
    digitalWrite(dice_pins[3], LOW);
    digitalWrite(dice_pins[4], LOW);
    digitalWrite(dice_pins[5], LOW);
    digitalWrite(dice_pins[6], HIGH);
    spin_step=0;

  }

  delay(spin_time);
  
  show_dice = true;
  
}

// show rolled value on dice leds
void dice(int value){
  // reset leds

        digitalWrite(dice_pins[0], LOW);
        digitalWrite(dice_pins[1], LOW);
        digitalWrite(dice_pins[2], LOW);
        digitalWrite(dice_pins[3], LOW);
        digitalWrite(dice_pins[4], LOW);
        digitalWrite(dice_pins[5], LOW);
        digitalWrite(dice_pins[6], LOW); 

  delay(1000);
  
  switch(value) {
    case 1:
      digitalWrite(dice_pins[0], LOW);
      digitalWrite(dice_pins[1], LOW);
      digitalWrite(dice_pins[2], LOW);
      digitalWrite(dice_pins[3], LOW);
      digitalWrite(dice_pins[4], LOW);
      digitalWrite(dice_pins[5], LOW);
      digitalWrite(dice_pins[6], HIGH);
      break;
    case 2:
      digitalWrite(dice_pins[0], HIGH);
      digitalWrite(dice_pins[1], LOW);
      digitalWrite(dice_pins[2], LOW);
      digitalWrite(dice_pins[3], LOW);
      digitalWrite(dice_pins[4], LOW);
      digitalWrite(dice_pins[5], HIGH);
      digitalWrite(dice_pins[6], LOW);
      break;
    case 3:
      digitalWrite(dice_pins[0], HIGH);
      digitalWrite(dice_pins[1], LOW);
      digitalWrite(dice_pins[2], LOW);
      digitalWrite(dice_pins[3], LOW);
      digitalWrite(dice_pins[4], LOW);
      digitalWrite(dice_pins[5], HIGH);
      digitalWrite(dice_pins[6], HIGH);
      break;
    case 4:
      digitalWrite(dice_pins[0], HIGH);
      digitalWrite(dice_pins[1], LOW);
      digitalWrite(dice_pins[2], HIGH);
      digitalWrite(dice_pins[3], HIGH);
      digitalWrite(dice_pins[4], LOW);
      digitalWrite(dice_pins[5], HIGH);
      digitalWrite(dice_pins[6], LOW);
      break;
    case 5:
      digitalWrite(dice_pins[0], HIGH);
      digitalWrite(dice_pins[1], LOW);
      digitalWrite(dice_pins[2], HIGH);
      digitalWrite(dice_pins[3], HIGH);
      digitalWrite(dice_pins[4], LOW);
      digitalWrite(dice_pins[5], HIGH);
      digitalWrite(dice_pins[6], HIGH);
      break;
    case 6:
      digitalWrite(dice_pins[0], HIGH);
      digitalWrite(dice_pins[1], HIGH);
      digitalWrite(dice_pins[2], HIGH);
      digitalWrite(dice_pins[3], HIGH);
      digitalWrite(dice_pins[4], HIGH);
      digitalWrite(dice_pins[5], HIGH);
      digitalWrite(dice_pins[6], LOW);
      break;
    default:
      break;
  }

  show_dice = false;

}
